// Logisim project pong_cpu.circ as structural Verilog
module FullAdder (
  input  A,
  input  B,
  input  Cin,
  output SUM,
  output COUT
);

  wire and_1_out, and_2_out, xor_1_out;

  xor xor_1 (xor_1_out, A, B);
  and and_1 (and_1_out, B, A);
  xor xor_2 (SUM, xor_1_out, Cin);
  and and_2 (and_2_out, Cin, xor_1_out);
  or or_1 (COUT, and_2_out, and_1_out);
endmodule
